# Fritzing sketch electronic_2 (saved by Fritzing 0.9.2b)
circuit board: 5.15913cm x 3.56159cm
breadboards: 1

parts:
  Pro_Micro1 = SparkFun Pro Micro
  Motor = female pin header, 4 pins [form="♀ (female)"]
  Motor_Power = female pin header, 2 pins [form="♀ (female)"]
  In_Connector = female pin header, 6 pins [form="♀ (female)"]
  Out_Connector = female pin header, 6 pins [form="♀ (female)"]
  R1 = Resistor [tolerance=±5% resistance=220 package=THT]

nets:
  N1: Pro_Micro1.TX0, In_Connector.pin5
  N2: Pro_Micro1.RX1, In_Connector.pin4
  GND: Pro_Micro1.GND, Motor_Power.pin2, In_Connector.pin1, Out_Connector.pin1
  N3: Pro_Micro1.2, Out_Connector.pin4
  N4: Pro_Micro1.3, Out_Connector.pin5
  N5: Pro_Micro1.4, Out_Connector.pin6
  N6: Pro_Micro1.10, Motor.pin4
  N7: Pro_Micro1.16, Motor.pin3
  N8: Pro_Micro1.14, Motor.pin2
  N9: Pro_Micro1.15, Motor.pin1
  5V: Pro_Micro1.VCC, Motor_Power.pin1, In_Connector.pin2, Out_Connector.pin2, R1.Pin_1
  N10: Pro_Micro1.RST, In_Connector.pin3, Out_Connector.pin3
  N11: In_Connector.pin6, R1.Pin_0

notes:
  Flip Display - 2019-04-27
  GND
  5V
  RESET
  TX
  RX
  Terminal
  RST
  TRM
  frett27@gmail.com
  IN1
  IN2
  IN3
  IN4

custom parts:
  SparkFun Pro Micro: The Pro Micro is similar to the Pro Mini except with an ATmega32U4 on board. The USB transceiver inside the 32U4 allows us to add USB connectivity on-board and do away with bulky external USB interface. Based on: https://github.com/unorthodox-engineers/unorthodox-arduino/blob/master/Unorthodox/fritzing/parts/Pro%20Micro.fzpz
